# Fritzing sketch pong (saved by Fritzing 1.0.4)
breadboards: 1

parts:
  Composant1 = Arduino Uno (Rev3) - ICSP
  HC-SR04_Sensor_1 = HC-SR04 Ultrasonic Distance Sensor
  HC-SR04_Sensor_2 = HC-SR04 Ultrasonic Distance Sensor
  Grove1 = Grove OLED 128x96

nets:
  N1: Composant1.A4/SDA, Grove1.SDA
  N2: Composant1.A5/SCL, Grove1.SCL
  N3: Composant1.D8, HC-SR04_Sensor_1.TRIG
  N4: Composant1.D9_PWM, HC-SR04_Sensor_2.ECHO
  N5: Composant1.D10_PWM/SS, HC-SR04_Sensor_2.TRIG
  N6: Composant1.D7, HC-SR04_Sensor_1.ECHO
  VCC: Composant1.5V, HC-SR04_Sensor_1.VCC, HC-SR04_Sensor_2.VCC, Grove1.VCC
  GND: Composant1.GND, HC-SR04_Sensor_1.GND, HC-SR04_Sensor_2.GND, Grove1.GND
